# Fritzing sketch MQTT433gateway-wemos (saved by Fritzing 0.9.3b)
circuit board: 2.56cm x 4.4cm
stripboards: 1

parts:
  D1 = Rectifier Diode [part_number=1N4001 package="300 mil [THT]"]
  Power_plug1 = Power plug
  C4 = Tantalum Capacitor [capacitance=0.33µF voltage=20V package="100 mil [THT, tantalum]"]
  C5 = Tantalum Capacitor [capacitance=0.1µF package="100 mil [THT, tantalum]"]
  U3 = RF-LINK_TX [package=rf-link_tx]
  ANT1 = Antenna
  ANT2 = Antenna
  D2 = Rectifier Diode [part_number=1N4148 package="300 mil [THT]"]
  R1 = Resistor [tolerance=±5% resistance=1k package=THT]
  U2 = RF-LINK_RX2 [package=rf-link_rx2]
  J3 = female pin header, 4 pins [form="♀ (female)"]
  J4 = female pin header, 4 pins [form="♀ (female)"]
  J1 = female pin header, 8 pins [form="♀ (female)"]
  J2 = female pin header, 8 pins [form="♀ (female)"]
  LED1 = LED - 5mm [color="Green (555nm)" package="5 mm [THT]"]
  WeMos_D1_Mini1 = WeMos D1 Mini
  J5 = female pin header, 4 pins [form="♀ (female)"]
  U4 = Voltage Regulator - 3.3V [package="TO220 [THT]"]

nets:
  12V: D1.cathode, C4.+, U3.+5V, J3.pin2, U4.input_voltage
  N1: D1.anode, Power_plug1.VCC
  GND: Power_plug1.GND, C4.-, C5.-, U3.GND, U2.GND, J3.pin4, J4.pin2, J4.pin3, J2.pin2, WeMos_D1_Mini1.G, J5.pin1, U4.GND
  5V: C5.+, U2.+5V, J4.pin4, J2.pin1, WeMos_D1_Mini1.5V, J5.pin4, U4.output_voltage
  ANT_TX: U3.ANT, ANT2.antenna_lead, J3.pin1
  #4/send: U3.DATA, J3.pin3, J2.pin5, WeMos_D1_Mini1.D2
  ANT_RX: ANT1.antenna_lead, U2.ANT, J4.pin1
  recv: D2.cathode, U2.DATA, J5.pin2
  #12: D2.anode, J1.pin4, WeMos_D1_Mini1.D6
  #0: R1.Pin_0, J2.pin4, WeMos_D1_Mini1.D3
  N2: R1.Pin_1, LED1.cathode
  3.3V: J1.pin1, LED1.anode, WeMos_D1_Mini1.3V3

notes:
  MQTT433gateway for WeMOS
  2016 by Puuu
  v0.1

custom parts:
  RF-LINK_RX2: RF Link receivers- WRL-8947, 8948, 8949, 8950
