# Fritzing sketch MQTT433gateway (saved by Fritzing 0.9.2b)
circuit board: 8.46667cm x 5.64444cm
stripboards: 1

parts:
  D1 = Rectifier Diode [part_number=1N4001 package="300 mil [THT]"]
  Power_plug1 = Power plug
  C4 = Tantalum Capacitor [capacitance=0.33µF voltage=20V package="100 mil [THT, tantalum]"]
  C5 = Tantalum Capacitor [capacitance=0.1µF package="100 mil [THT, tantalum]"]
  U3 = RF-LINK_TX [package=rf-link_tx]
  ANT1 = Antenna
  ANT2 = Antenna
  D2 = Rectifier Diode [part_number=1N4148 package="300 mil [THT]"]
  R1 = Resistor [tolerance=±5% resistance=1k package=THT]
  LED1 = LED - 5mm [color="Green (555nm)" package="5 mm [THT]"]
  U2 = RF-LINK_RX2 [package=rf-link_rx2]
  J1 = female pin header, 10 pins [form="♀ (female)"]
  J2 = female pin header, 10 pins [form="♀ (female)"]
  J3 = female pin header, 4 pins [form="♀ (female)"]
  J4 = female pin header, 4 pins [form="♀ (female)"]
  J5 = female pin header, 4 pins [form="♀ (female)"]
  Part1 = Adafruit HUZZAH ESP8266 [part_number="Adafruit #2471"]
  IC1 = Voltage Regulator [package=78xxl]

nets:
  12V: D1.cathode, C4.+, U3.+5V, J3.pin2, IC1.IN
  N1: D1.anode, Power_plug1.VCC
  GND: Power_plug1.GND, C4.-, C5.-, U3.GND, U2.GND, J1.pin1, J2.pin1, J3.pin4, J4.pin2, J4.pin3, J5.pin1, Part1.GND, IC1.GND
  5V: C5.+, U2.+5V, J1.pin3, J4.pin4, J5.pin4, Part1.VIN, IC1.OUT
  ANT_TX: U3.ANT, ANT2.antenna_lead, J3.pin1
  #4/send: U3.DATA, J2.pin7, J3.pin3, Part1.GPIO4
  ANT_RX: ANT1.antenna_lead, U2.ANT, J4.pin1
  recv: D2.cathode, U2.DATA, J5.pin2
  #12: D2.anode, J1.pin5, Part1.GPIO12
  #0: R1.Pin_0, J2.pin6, Part1.GPIO0
  N2: R1.Pin_1, LED1.cathode
  3.3V: LED1.anode, J2.pin3, Part1.3.3V
  N3: J1.pin2, Part1.VBAT
  N4: J1.pin4, Part1.GPIO13
  N5: J1.pin6, Part1.GPIO14
  N6: J1.pin7, Part1.GPIO16
  N7: J1.pin8, Part1.EN
  N8: J1.pin9, Part1.ADC
  N9: J1.pin10, Part1.RESET
  N10: J2.pin2, Part1.LDO
  N11: J2.pin4, Part1.GPIO15
  N12: J2.pin5, Part1.GPIO2
  N13: J2.pin8, Part1.GPIO5
  N14: J2.pin9, Part1.RX
  N15: J2.pin10, Part1.TX

custom parts:
  RF-LINK_RX2: RF Link receivers- WRL-8947, 8948, 8949, 8950
  Adafruit HUZZAH ESP8266: Add Internet to your next project with an adorable, bite-sized WiFi microcontroller, at a price you like! The ESP8266 processor from Espressif is an 80 MHz microcontroller with a full WiFi front-end (both as client and access point) and TCP/IP stack with DNS support as well. While this chip has been very popular, its also been very difficult to use. Most of the low cost modules are not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
